# Fritzing sketch beadando_sketch_10_12 (saved by Fritzing 0.9.3b)
breadboards: 1

parts:
  U2 = RELAY [package=relay-jzc]
  U3 = RELAY [package=relay-jzc]
  U4 = RELAY [package=relay-jzc]
  Part1 = Arduino Uno (Rev3)
  INFRA_VÖRÖS_VEVŐ = TSOP312.., 314.. [package=THT]
  BLUETOOTH = Bluetooth HC-05 Macho
  RIASZTÓ = Piezo Speaker
  FENYERO_SZENZOR = PHOTOCELL [package=photocell]
  HOMERSEKLET_SZENZOR = Camdenboss CTB0158-4 [part_number=CTB0158-4 package=THT]
  BELTERI_VILAGITAS = smd LED [color="Red (633nm)" package="0805 [SMD]"]
  R2 = Resistor [tolerance=±5% resistance=220 package="0402 [SMD]"]  # not connected
  R3 = Resistor [tolerance=±5% resistance=220 package="0402 [SMD]"]  # not connected
  R4 = Resistor [tolerance=±5% resistance=220 package="0603 [SMD]"]
  KULTERI_VILAGITAS = LED - 5mm [color="Red (633nm)" package="5 mm [THT]"]
  R5 = Resistor [tolerance=±5% resistance=220 package="0805 [SMD]"]  # not connected
  TERMOSZTAT = smd LED [color="Red (633nm)" package="0603 [SMD]"]
  LCD_KIJELZŐ = Camdenboss CTB0158-4 [part_number=CTB0158-4 package=THT]
  MOZGASERZEKELO = JST-B3P-VH [part_number=JST-B3P-VH package=THT]

nets:
  N1: U2.COIL1, Part1.D13/SCK
  5V: U3.NC, Part1.5V, INFRA_VÖRÖS_VEVŐ.Vs, BLUETOOTH.VCC, FENYERO_SZENZOR.P$1, HOMERSEKLET_SZENZOR.terminal_2, LCD_KIJELZŐ.terminal_3, MOZGASERZEKELO.pin2
  N2: U3.COIL1, Part1.D12/MISO
  N3: U4.COIL1, Part1.D8
  N4: Part1.A0, HOMERSEKLET_SZENZOR.terminal_4
  N5: Part1.A4/SDA, LCD_KIJELZŐ.terminal_2
  N6: Part1.A5/SCL, LCD_KIJELZŐ.terminal_1
  N7: Part1.D10_PWM/SS, RIASZTÓ.pin2
  N8: Part1.D11_PWM/MOSI, INFRA_VÖRÖS_VEVŐ.Data
  GND: Part1.GND, INFRA_VÖRÖS_VEVŐ.GND, BLUETOOTH.GND, RIASZTÓ.pin1, HOMERSEKLET_SZENZOR.pin3, BELTERI_VILAGITAS.cathode, R4.Pin_1, KULTERI_VILAGITAS.cathode, TERMOSZTAT.cathode, LCD_KIJELZŐ.terminal_4, MOZGASERZEKELO.pin3
  N9: Part1.D0/RX, BLUETOOTH.TXD
  N10: Part1.D1/TX, BLUETOOTH.RXD
  N11: Part1.D3_PWM, HOMERSEKLET_SZENZOR.terminal_1
  N12: Part1.D7, MOZGASERZEKELO.pin1
  N13: FENYERO_SZENZOR.P$2, R4.Pin_0
